# Fritzing sketch Sketch (saved by Fritzing 0.9.3b)
breadboards: 1

parts:
  Atmega1 = ATmega328 [package=tqfp]
  R1 = TRIMPOT [package=3362u-2]
  Part1 = Motor Driver 1A Dual TB6612FNG
  M1 = DC Motor
  S1 = Pushbutton [package="[SMD]"]
  LED1 = smd LED [color="Red (633nm)" package="0603 [SMD]"]
  R2 = Resistor [tolerance=±5% resistance=220 package="0402 [SMD]"]

nets:
  GND: Atmega1.GND, R1.CW, Part1.GND, LED1.anode, R2.Pin_0
  VCC: Atmega1.VCC, Atmega1.PC1(ADC1), R1.CCW, Part1.VCC, Part1.STBY, S1.Pin_3, S1.Pin_4, R2.Pin_1
  N1: Atmega1.PB1(OC1A), Part1.PWMA
  N2: Atmega1.PC0(ADC0), R1.WIPER
  N3: Atmega1.PD0(RXD), Part1.AIN1
  N4: Atmega1.PD1(TXD), Part1.AIN2
  N5: Part1.A02, M1.pin_1
  N6: Part1.A01, M1.pin_2
  N7: S1.Pin_1, S1.Pin_2

notes:
  Note:
  The red component represents the TB6122FNG. Also, the MCU used in this schematic is the Atmega328 NOT the Atmega328P Xplained Mini Board.
