# Fritzing sketch Sketch (saved by Fritzing 0.9.3b)
breadboards: 1

parts:
  Atmega1 = ATmega328 [package=tqfp]
  M2 = Dagu DGServo 9g (Pan and tilt) [part_number=RS001B]
  R1 = TRIMPOT [package=trimpot_pth_s3_lock]
  M1 = Stepper Motor - Unipolar
  IC1 = ULN2003A [package="DIP16 [THT]"]

nets:
  GND: Atmega1.GND, M2.gnd, R1.CCW
  VCC: Atmega1.VCC, M2.vcc, R1.CW
  N1: Atmega1.PB1(OC1A), M2.pulse
  N2: Atmega1.PC0(ADC0), R1.WIPER
  N3: M1.COMMON_1, IC1.Out_2
  N4: M1.C, IC1.Out_3
  N5: M1.B, IC1.Out_4
  N6: M1.COMMON_2, M1.D, IC1.COM_-_Common
