# Fritzing sketch Sketch (saved by Fritzing 0.9.3b)
breadboards: 1

parts:
  Part1 = InvenSense MPU6050
  Atmega1 = ATmega328 [package=tqfp]
  Part2 = FTDI Basic Programmer

nets:
  VCC: Part1.VCC, Atmega1.VCC
  N1: Part1.SCL, Atmega1.PC5(ADC5_SCL)
  N2: Part1.SDA, Atmega1.PC4(ADC4_SDA)
  GND: Atmega1.GND, Part2.GND
  N3: Atmega1.PD0(RXD), Part2.TXO
  N4: Atmega1.PD1(TXD), Part2.RXI

notes:
  Note: This is the schematic for the ATMega328 not the ATMega328p
