# Fritzing sketch Sketch (saved by Fritzing 0.9.3b)

parts:
  Atmega1 = ATmega328 [package=tqfp]
  U1 = ESP8266 WiFi Module [part_number=ESP8266]

nets:
  GND: Atmega1.GND, U1.GND
  VCC: Atmega1.VCC, U1.VCC
  N1: Atmega1.PD0(RXD), U1.TXD
  N2: Atmega1.PD1(TXD), U1.RXD

notes:
  Since some of the components are missing in frtizing, it is important to note that the ESP8266 represents the ESP-01 Black 8Mbit Module. And the Atmega328 represents the Atmega 328P Xplained Mini. There is also no ESP-01 Adapter which connects the ESP-01 Module to the Atmega 328P.
